# Fritzing sketch wiring-withANano (saved by Fritzing 1.0.6)
breadboards: 5

parts:
  A1 = Waveshare ESP32-Pico  # not connected
  M1 = RPlidar A2M8 [package=THT]  # not connected
  DC_Mot_Enc1 = DC Motor with two-phase hall-encoder [part_number=VT-E-G25A-06-177E]  # not connected
  Part1 = Arduino Nano (Rev3.0)
  DC_Mot_Enc2 = DC Motor with two-phase hall-encoder [part_number=VT-E-G25A-06-177E]  # not connected
  DC_Mot_Enc3 = DC Motor with two-phase hall-encoder [part_number=VT-E-G25A-06-177E]  # not connected
  DC_Mot_Enc4 = DC Motor with two-phase hall-encoder [part_number=VT-E-G25A-06-177E]  # not connected
  HC-SR04_Sensor_1 = HC-SR04 Ultrasonic Distance Sensor
  U1 = LIPO-1000mAh [package=lipo-1000]
  M2 = RioRand LM2596
  X1 = USB Connectors [package=usb-microb]  # not connected
  M3 = fc-51 [package=THT]
  M4 = fc-51 [package=THT]
  A3 = Sparkfun sen18642  # not connected
  Part3 = InvenSense MPU6050
  A4 = Hi-link HLK-LD2410C  # not connected
  A5 = Jetson Nano  # not connected
  U2 = LIPO-2000mAh [package=lipo-2000]  # not connected
  Part6 = I2C level shifter bidirectional
  U3 = LIPO-1000mAh [package=lipo-1000]
  M5 = RioRand LM2596
  X2 = USB Connectors [package=usb-microb]  # not connected
  M6 = fc-51 [package=THT]
  M7 = fc-51 [package=THT]
  A6 = Sparkfun sen18642
  Part7 = InvenSense MPU6050
  A7 = Hi-link HLK-LD2410C
  U4 = LIPO-2000mAh [package=lipo-2000]  # not connected
  Part8 = I2C level shifter bidirectional  # not connected
  HC-SR04_Sensor_2 = HC-SR04 Ultrasonic Distance Sensor
  M8 = RPlidar A2M8 [package=THT]  # not connected
  DC_Mot_Enc5 = DC Motor with two-phase hall-encoder [part_number=VT-E-G25A-06-177E]
  DC_Mot_Enc6 = DC Motor with two-phase hall-encoder [part_number=VT-E-G25A-06-177E]
  DC_Mot_Enc7 = DC Motor with two-phase hall-encoder [part_number=VT-E-G25A-06-177E]
  DC_Mot_Enc8 = DC Motor with two-phase hall-encoder [part_number=VT-E-G25A-06-177E]
  Part9 = Arduino Nano (Rev3.0)
  Mod1 = Raspberry Pi Pico W  # not connected
  JP1 = Header 5x2 [package=2x5-ra]
  JP2 = Header 5x2 [package=2x5-ra]  # not connected
  JP3 = Header 5x2 [package=2x5-ra]
  JP4 = Header 5x2 [package=2x5-ra]
  J1 = STARBOARD_GND [package=starboard_ground_small2]
  J2 = STARBOARD_GND [package=starboard_ground_small2]
  J3 = STARBOARD_GND [package=starboard_ground_small2]
  Mod2 = Raspberry Pi Pico W
  JP5 = Header 5x2 [package=2x5-ra]
  JP6 = Header 5x2 [package=2x5-ra]
  JP7 = Header 5x2 [package=2x5-ra]
  JP8 = Header 5x2 [package=2x5-ra]
  J4 = STARBOARD_GND [package=starboard_ground_small2]
  J5 = STARBOARD_GND [package=starboard_ground_small2]
  U5 = LIPO-1000mAh [package=lipo-1000]
  M9 = RioRand LM2596
  M10 = fc-51 [package=THT]
  M11 = fc-51 [package=THT]
  A8 = Sparkfun sen18642
  Part10 = InvenSense MPU6050
  A9 = Hi-link HLK-LD2410C
  U6 = LIPO-2000mAh [package=lipo-2000]  # not connected
  Part11 = I2C level shifter bidirectional
  HC-SR04_Sensor_3 = HC-SR04 Ultrasonic Distance Sensor
  M12 = RPlidar A2M8 [package=THT]  # not connected
  DC_Mot_Enc9 = DC Motor with two-phase hall-encoder [part_number=VT-E-G25A-06-177E]
  DC_Mot_Enc10 = DC Motor with two-phase hall-encoder [part_number=VT-E-G25A-06-177E]
  DC_Mot_Enc11 = DC Motor with two-phase hall-encoder [part_number=VT-E-G25A-06-177E]
  DC_Mot_Enc12 = DC Motor with two-phase hall-encoder [part_number=VT-E-G25A-06-177E]
  J8 = Camdenboss CTB0158-4 [part_number=CTB0158-4 package=THT]
  DC_Mot_Enc13 = DC Motor with two-phase hall-encoder [part_number=VT-E-G25A-06-177E]
  DC_Mot_Enc16 = DC Motor with two-phase hall-encoder [part_number=VT-E-G25A-06-177E]  # not connected
  J16 = STARBOARD_GND [package=starboard_ground_small2]
  J6 = STARBOARD_GND [package=starboard_ground_small2]

nets:
  N1: Part1.D1/TX, Part6.HV2
  N2: Part1.D0/RX, Part6.HV1
  GND: Part1.GND, HC-SR04_Sensor_1.GND, M3.pin2, Part3.GND, Part6.GND
  VCC: Part1.5V, HC-SR04_Sensor_1.VCC, M3.pin3, Part3.VCC, Part6.HV
  N3: Part1.A5, M4.pin1
  N4: Part1.3V3, Part6.LV
  N5: U1.+, M2.Pin_1
  N6: U1.-, M2.Pin_2
  N7: U3.+, M5.Pin_1
  N8: U3.-, M5.Pin_2, A6.Pin_5, A6.Pin_11, A7.Pin_4, J2.MOUNT
  N9: M6.pin1, Part9.A1
  N10: M6.pin2, JP1.6
  N11: M6.pin3, M7.pin3, A7.Pin_5, Part9.5V
  GND_2: M7.pin2, Part7.GND, HC-SR04_Sensor_2.GND, DC_Mot_Enc5.pin2, DC_Mot_Enc7.pin2, Part9.GND, J1.MOUNT
  N12: A6.Pin_6, JP1.1
  N13: A6.Pin_7, JP4.1
  N14: A6.Pin_8, JP4.3
  VCC_2: Part7.VCC, HC-SR04_Sensor_2.VCC, Part9.3V3
  N15: A7.Pin_1, JP1.8
  N16: A7.Pin_2, JP1.10
  N17: DC_Mot_Enc5.pin3, JP4.4
  N18: DC_Mot_Enc5.pin4, JP4.2
  N19: DC_Mot_Enc6.pin2, DC_Mot_Enc8.pin2, J3.MOUNT
  N20: DC_Mot_Enc6.pin3, JP4.10
  N21: DC_Mot_Enc6.pin4, JP4.8
  N22: DC_Mot_Enc7.pin3, JP3.1
  N23: DC_Mot_Enc7.pin4, JP3.3
  N24: DC_Mot_Enc8.pin3, JP3.4
  N25: DC_Mot_Enc8.pin4, JP3.2
  N26: Mod2.pin_30, JP6.8
  N27: Mod2.pin_31, JP6.9, JP6.10
  N28: Mod2.pin_33, Mod2.pin_42, JP7.2
  N29: Mod2.pin_34, JP7.3, JP7.4, JP7.5, Part11.LV2
  N30: Mod2.pin_36, JP7.8
  N31: Mod2.pin_37, JP7.10
  N32: Mod2.pin_39, JP8.2
  N33: Mod2.pin_40, JP8.4
  N34: JP5.1, A8.Pin_7, Part10.SDA
  N35: JP5.2, DC_Mot_Enc9.pin4
  N36: JP5.3, A8.Pin_8, Part10.SCL
  N37: JP5.4, JP5.6, DC_Mot_Enc9.pin3
  N38: JP5.7, JP5.8, JP5.9, DC_Mot_Enc10.pin4
  N39: JP5.10, DC_Mot_Enc10.pin3
  N40: JP6.1, DC_Mot_Enc11.pin3
  N41: JP6.2, DC_Mot_Enc12.pin4
  N42: JP6.3, JP6.5, DC_Mot_Enc11.pin4
  N43: JP6.4, JP6.6, DC_Mot_Enc12.pin3
  N44: JP6.7, Part11.LV4
  N45: JP7.1, Part11.LV3
  N46: JP7.7, Part11.LV1
  N47: JP8.1, A8.Pin_6, Part10.VCC, Part11.LV
  N48: JP8.8, A9.Pin_1
  N49: JP8.10, A9.Pin_2
  N50: J4.MOUNT, DC_Mot_Enc9.pin2, DC_Mot_Enc10.pin2, DC_Mot_Enc11.pin2, DC_Mot_Enc12.pin2
  N51: J5.MOUNT, A9.Pin_4
  N52: U5.+, M9.Pin_1
  N53: U5.-, M9.Pin_2, M9.Pin_4, M10.pin2, Part11.GND
  N54: M9.Pin_3, M10.pin3, M11.pin3, A9.Pin_5
  N55: M10.pin1, Part11.HV4
  N56: M11.pin1, Part11.HV1
  N57: M11.pin2, HC-SR04_Sensor_3.GND, J6.MOUNT
  N58: A8.Pin_5, J16.MOUNT
  N59: Part11.HV2, HC-SR04_Sensor_3.TRIG
  N60: Part11.HV, HC-SR04_Sensor_3.VCC
  N61: Part11.HV3, HC-SR04_Sensor_3.ECHO
  N62: DC_Mot_Enc9.pin5, J8.pin4
  N63: DC_Mot_Enc10.pin5, J8.pin2
  N64: DC_Mot_Enc11.pin5, J8.pin1
  N65: DC_Mot_Enc12.pin5, J8.pin3
  N66: DC_Mot_Enc13.pin5, DC_Mot_Enc13.pin6

notes:
  REd=5V/6V power,
  Pink = Signal,
  Black = ground, Orange = 3.3V power
  green/yellow = I2C-ish signal pairs
  SR04 is 5V. Fish sensor is 5V
  motors - encoder can be 3.3-5V. Output will be according to input
  Vl53L5CX is 3.3V power and
  https://learn.sparkfun.com/tutorials/qwiic-tof-imager---vl53l5cx-hookup-guide
  LD2450 power is 5V,200mA. It's Serial port (UART?) TxRx is 3.3V, default baud 256k
  MPU6050 is 3.3 or 5V as per power supply
  ESP32-Pico pins GP39 and GND are interchanged in this model. But onreal piece they are as per datasheet
  Nano V3 is 5V device . Power will be from micro- USB at 5V from the Jetson
  motors - encoder can be 3.3-5V. Output will be according to input
  Red = motor+
  White = Motor-
  Yellow - signal feedback,
  Green = signal feedback
  Blue = encoder supply +
  Black = encoder supply -
  Nano V3 is 5V device . Power will be from micro- USB at 5V from the Jetson
  SDA A4(23), SCL A5(24)
  motors - encoder supply can be 3.3-5V. Output will be according to input
  Red = motor+
  White = Motor-
  Yellow - signal feedback,
  Green = signal feedback
  Blue = encoder supply +
  Black = encoder supply -
  Here, the Arduino Nano seems a wasted component causing excess wiring. SO pausing this and drawing teh one on right
  1. LD06 LiDAR Connection (UART)
  The LD06 communicates via serial (UART). It typically requires 5V power but uses 3.3V logic for data, which matches the Jetson's logic level perfectly.
  Protocol: UART (8N1, 230400 baud)
  Jetson Device Path: /dev/ttyTHS1 (Primary UART)
  Signal
  LD06 Wire Color (Typ.)
  Jetson Orin Nano Pin
  Pin Function
  5V
  Red
  Pin 4
  5V Power
  GND
  Black
  Pin 6
  Ground
  TX
  Yellow (or Green)
  Pin 10
  UART1_RX (Receive)
  PWM
  Blue (or White)
  Not Connected
  Motor Control*
  r note here]
  2. I2C Device Connection
  The Jetson Orin Nano has two main I2C buses on the header. Bus 7 is the standard recommended bus for external sensors.
  Jetson Device Path: /dev/i2c-7 (Bus 7) or sometimes /dev/i2c-1 (Bus 1) depending on OS version, but physically these are the pins:
  Signal
  I2C Device Pin
  Jetson Orin Nano Pin
  Pin Function
  SDA
  SDA
  Pin 3
  I2C_2_SDA (Bus 7)
  SCL
  SCL
  Pin 5
  I2C_2_SCL (Bus 7)
  VCC
  VCC
  Pin 1 (3.3V) or Pin 2 (5V)
  Power (Check your device specs)
  GND
  GND
  Pin 9
  Ground
  3. ILI9341 Display Connection (SPI)
  The ILI9341 driver requires a 4-wire SPI connection plus GPIOs for Reset (RST) and Data/Command (DC).
  Protocol: SPI (Mode 0)
  Jetson Device Path: /dev/spidev0.0
  Important: You must enable SPI using the jetson-io tool (see instructions below).
  Signal
  ILI9341 Pin
  Jetson Orin Nano Pin
  Pin Function
  VCC
  VCC
  Pin 2
  5V Power (Most modules have 3.3V regulator)
  GND
  GND
  Pin 14
  Ground
  CS
  CS
  Pin 24
  SPI0_CS0 (Chip Select)
  RESET
  RST
  Pin 22
  GPIO (can use other free GPIO)
  DC
  DC/RS
  Pin 18
  GPIO (can use other free GPIO)
  MOSI
  MOSI/SDA
  Pin 19
  SPI0_MOSI (Master Out)
  SCK
  SCK/CL
  Pin 23
  SPI0_SCK (Clock)
  LED
  LED/BLK
  Pin 1
  3.3V (Always On) or use GPIO for dimming
  MISO
  MISO
  Pin 21
  SPI0_MISO (Master In)
  Critical Step: Enabling the Pins
  By default, the SPI pins on the Jetson Orin Nano might be disabled or set to GPIO mode. To ensure they work:
  Open a terminal on the Jetson.
  Run the configuration tool: sudo /opt/nvidia/jetson-io/jetson-io.py
  Select Configure Jetson 40pin Header.
  Select Configure header pins manually.
  Ensure SPI1 (pins 19, 21, 23, 24, 26) is checked/enabled.
  Save and Reboot the system.

custom parts:
  RPlidar A2M8: .The RPLIDAR A2 is the next generation low cost 360 degree 2D laser scanner (LIDAR) solution developed by SLAMTEC. It can take up to 4000 samples of laser ranging per second with high rotation speed. And equipped with SLAMTEC patented OPTMAG technology, it breakouts the life limitation of traditional LIDAR system so as to work stably for a long time.
  Sparkfun sen18642: The SparkFun Qwiic ToF Imager is built around VL53L5CX from ST Electronics; a state of the art, Time-of-Flight (ToF), multizone ranging sensor.
  Hi-link HLK-LD2410C: LD2410C is a high-sensitivity 24GHz human presence status sensing module. bb reversed for on perfboard in breadboard.
  Raspberry Pi Pico W: Raspberry Pi Pico W. Based around the RP2040 microcontroller the Pico W is a low cost microcontroller device bringing Raspberry Pi quality, cost, and easy of use to the microcontroller space. The areas marked KEEPOUT in pcb silkscreen should not have traces running through them to avoid shorts on a soldered in module!
